# Fritzing sketch Plant sensor 1.0 (saved by Fritzing 0.9.3b)
breadboards: 1

parts:
  DS1 = DS18B20 1-Wire Temperature Sensor [part_number=DS18B20]
  RHT1 = Humidity and Temperature Sensor RHT03
  Chirp!_Soil_Moisture_Sensor1 = Chirp! Soil Moisture Sensor v2.7.3
  Chirp!_Soil_Moisture_Sensor3 = Chirp! Soil Moisture Sensor v2.7.3
  R1 = Resistor [tolerance=±5% resistance=10k package="2512 [SMD]"]
  R2 = Resistor [tolerance=±5% resistance=10k package="2512 [SMD]"]
  Mod1 = Raspberry Pi Pico
  Chirp!_Soil_Moisture_Sensor2 = Chirp! Soil Moisture Sensor v2.7.3
  Part1 = Waveshare Pico OLED 1.3

nets:
  N1: DS1.GND, RHT1.GND_2, Chirp!_Soil_Moisture_Sensor1.pin_5, Chirp!_Soil_Moisture_Sensor3.pin_5, Mod1.pin_23, Mod1.pin_38, Chirp!_Soil_Moisture_Sensor2.pin_5, Part1.pin_33, Part1.pin_38
  N2: DS1.DQ, R1.Pin_0, Mod1.pin_21
  N3: DS1.VDD, R1.Pin_1
  N4: RHT1.Vcc, R2.Pin_0
  N5: RHT1.Data-signal, R2.Pin_1, Mod1.pin_4, Part1.pin_37
  N6: Chirp!_Soil_Moisture_Sensor1.Pin_1, Chirp!_Soil_Moisture_Sensor3.Pin_1, Mod1.pin_36, Chirp!_Soil_Moisture_Sensor2.Pin_1
  N7: Chirp!_Soil_Moisture_Sensor1.pin_3, Mod1.pin_26
  N8: Chirp!_Soil_Moisture_Sensor3.pin_3, Mod1.pin_29
  N9: Mod1.pin_11, Part1.pin_11, Part1.pin_30
  N10: Mod1.pin_12, Part1.pin_12, Part1.pin_29
  N11: Mod1.pin_14, Part1.pin_14, Part1.pin_27
  N12: Mod1.pin_15, Part1.pin_15, Part1.pin_26
  N13: Mod1.pin_16, Part1.pin_16, Part1.pin_25
  N14: Mod1.pin_17, Part1.pin_17, Part1.pin_24
  N15: Mod1.pin_20, Part1.pin_20, Part1.pin_21
  N16: Mod1.pin_22, Part1.pin_22
  N17: Mod1.pin_27, Chirp!_Soil_Moisture_Sensor2.pin_3
  N18: Mod1.pin_39, Part1.pin_39

custom parts:
  Raspberry Pi Pico: Raspberry Pi Pico. Based around the RP2040 microcontroller the Pico is a low cost microcontroller device bringing Raspberry Pi quality, cost, and easy of use to the microcontroller space. Jan 2021, Split part in to two versions: tht (this one) and SMD. This one will drill holes for a .1 in header in pcb to allow plugging in the module as well as providing pads to solder the module to the top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
  Waveshare Pico OLED 1.3: This 1.3inch OLED display module is designed for Raspberry Pi Pico, 64x128 pixels, support PSI/I2C interface.
